# Fritzing sketch RPi_USBtoTLL_complete (saved by Fritzing 0.9.3b)

parts:
  Bauteil1 = XBee USB Mini Adapter
  Gesture_Sensor = ZX Sensor [chip_label=IC package="DIP (Dual Inline) [THT]"]
  Raspberry_Pi_1 = Raspberry Pi 3 [part_number=RPI-3-V1.2]

nets:
  N1: Bauteil1.RXD, Raspberry_Pi_1.GPIO14
  N2: Bauteil1.TXD, Raspberry_Pi_1.GPIO15
  GND: Bauteil1.GND, Gesture_Sensor.pin5, Raspberry_Pi_1.GND
  5V: Bauteil1.5V, Raspberry_Pi_1.5V
  N3: Gesture_Sensor.pin4, Raspberry_Pi_1.3V3
  N4: Gesture_Sensor.pin8, Raspberry_Pi_1.GPIO3
  N5: Gesture_Sensor.pin_9, Raspberry_Pi_1.GPIO2

custom parts:
  ZX Sensor: A DIP stand-in part for whatever IC you want. With 8 pins on a 300mil dual inline package (DIP) footprint.
